# Fritzing sketch pointless plan (saved by Fritzing 0.9.3b)
breadboards: 1

parts:
  Part1 = Arduino Uno (Rev3)
  S1 = Square Pushbutton
  LED1 = smd LED [color="Red (633nm)" package="0603 [SMD]"]
  J1 = Piezo Speaker
  R1 = Resistor [tolerance=±5% resistance=220 package="2512 [SMD]"]

nets:
  N1: Part1.D13/SCK, LED1.anode
  N2: Part1.GND, LED1.cathode, J1.pin2, R1.Pin_0
  N3: Part1.D3_PWM, J1.pin1
  N4: Part1.D7, S1.leg0, R1.Pin_1
  N5: Part1.5V, S1.leg1
